// Logisim project HalfAdder.circ as structural Verilog: 1 circuit, main circuit main
module main (
  input  A,
  input  B,
  output Sum,
  output Carry
);

  and and_1 (Carry, B, A);
  xor xor_1 (Sum, A, B);
endmodule
